# Fritzing sketch flipando (saved by Fritzing 0.8.7b)
circuit board: 4.03746cm x 3.05054cm
breadboards: 1

parts:
  U1 = AD5206 Digital Potentiometer [maximum_resistance=10kΩ package="DIP28 [THT]"]
  IC1 = IC, DIP package, 8 pins [chip_label=JOTAs]
  DIN1 = DIN-5 jack (MIDI) [package=THT]

nets:
  N1: U1.A6, IC1.pin6
  N2: U1.W6, IC1.pin5
  N3: U1.B6, IC1.pin7
  N4: U1.CS, IC1.pin8
  N5: U1.Vdd, IC1.pin4
  N6: U1.SDI, IC1.pin3
  N7: U1.CLK, IC1.pin2
  N8: U1.Vss, IC1.pin1
  N9: U1.W2, DIN1.3
  N10: U1.B2, DIN1.5
  N11: U1.A4, DIN1.2
  N12: U1.W4, DIN1.4
  N13: U1.B4, DIN1.1
