# Fritzing sketch midiberry (saved by Fritzing 0.8.7b)
circuit board: 6.26136cm x 3.10859cm
breadboards: 1

parts:
  MIDI_OUT = DIN-5 jack (MIDI) [package=THT]
  MIDI_IN = DIN-5 jack (MIDI) [package=THT]
  MIDI_THRU = DIN-5 jack (MIDI) [package=THT]
  Raspberry_Pi_B_rev1 = Raspberry Pi B rev2
  Inversores = SN74LS14N [package="DIP14 [THT]"]
  Optoacoplador = OPTO_DARL_6N138S [package=8-smd]

nets:
  N1: MIDI_OUT.3, Raspberry_Pi_B_rev1.5V
  N2: MIDI_OUT.5, Inversores.VCC
  N3: MIDI_OUT.2, Inversores.6Y
  N4: MIDI_OUT.4, Inversores.5Y
  N5: MIDI_OUT.1, Inversores.4A
  GND: MIDI_OUT.GND, MIDI_IN.GND, MIDI_THRU.GND, Raspberry_Pi_B_rev1.GND, Inversores.1A
  N6: MIDI_IN.5, Optoacoplador.A
  N7: MIDI_IN.4, Inversores.GND
  N8: MIDI_IN.1, Inversores.3Y
  N9: MIDI_THRU.2, Optoacoplador.VCC
  N10: MIDI_THRU.4, Optoacoplador.VOUT
  N11: MIDI_THRU.1, Optoacoplador.GND
  N12: Raspberry_Pi_B_rev1.GPIO_14, Inversores.2A
  N13: Raspberry_Pi_B_rev1.GPIO_15, Inversores.1Y
